# Fritzing sketch Watch Arduino Mega 128x64 LCD RTC  (saved by Fritzing 0.9.6b)
breadboards: 1

parts:
  Part1 = Arduino Mega 2560 (Rev3)
  GLCD_128x1 = 128 x 64 Graphic LCD
  S1 = Momentary Switch [package=ksa_sealed_tac_switch]
  S2 = Momentary Switch [package=ksa_sealed_tac_switch]
  S3 = Momentary Switch [package=ksa_sealed_tac_switch]
  S4 = Momentary Switch [package=ksa_sealed_tac_switch]
  S5 = Momentary Switch [package=ksa_sealed_tac_switch]
  J1 = Piezo Speaker
  PCB2 = RTC_DS1302_module

nets:
  N1: Part1.A1, J1.pin2
  N2: Part1.A2, GLCD_128x1.17_RST
  N3: Part1.A3, GLCD_128x1.4_D/I
  N4: Part1.A4, GLCD_128x1.5_R/W
  N5: Part1.A5, GLCD_128x1.6_Enable
  N6: Part1.D12_PWM, S2.1, S2.2
  N7: Part1.D11_PWM, S4.1, S4.2
  N8: Part1.D10_PWM, S3.3, S3.4
  N9: Part1.D9_PWM, S5.3, S5.4
  N10: Part1.D8_PWM, S1.3, S1.4
  N11: Part1.3V3, GLCD_128x1.19_A(+)
  5V: Part1.5V, GLCD_128x1.2_Vdd, PCB2.VCC
  GND: Part1.GND, GLCD_128x1.1_Vss, GLCD_128x1.20_K(-), S1.1, S1.2, S2.3, S2.4, S3.1, S3.2, S4.3, S4.4, S5.1, S5.2, J1.pin1, PCB2.GND
  N12: Part1.D5_PWM, PCB2.CLK
  N13: Part1.D6_PWM, PCB2.DAT
  N14: Part1.D7_PWM, PCB2.RST

custom parts:
  RTC_DS1302_module: Arduino module DS1302 SPI Real Time Clock
